# Fritzing sketch Big power supply (PSU) (saved by Fritzing 0.9.10b)
circuit board: 12.3896cm x 6.096cm
breadboards: 1

parts:
  D1 = Rectifier Diode [part_number=1N4001 package="300 mil [THT]"]
  D2 = Rectifier Diode [part_number=1N4001 package="300 mil [THT]"]
  D3 = Rectifier Diode [part_number=1N4001 package="300 mil [THT]"]
  D4 = Rectifier Diode [part_number=1N4001 package="300 mil [THT]"]
  C1 = Electrolytic Capacitor [capacitance=2.2mF voltage=35V package="100 mil [THT, electrolytic]"]
  C2 = Electrolytic Capacitor [capacitance=2.2mF voltage=35V package="100 mil [THT, electrolytic]"]
  7805CT = Voltage Regulator - 5V [package="TO220 [THT]"]
  LM317K = Voltage Regulator - Variable [package="TO220 [THT]"]
  C3 = Tantalum Capacitor [capacitance=0.1µF voltage=35V package="B 3528 [SMD, tantalum]"]
  Fuse1 = Fuse with Handler [part_number=Htc-15m]
  Part1 = Taiway 100-SP-X-T1 SPDT Miniature Toggle Switch [part_number=100-SP-X-T1-0-0-B1-M1 package=THT]
  Part1_2 = Taiway 100-SP-X-T1 SPDT Miniature Toggle Switch [part_number=100-SP-X-T1-0-0-B1-M1 package=THT]
  R1 = Rotary Potentiometer (Large) [maximum_resistance=10kΩ knob_status=50% power=0.5W package=THT]
  U1 = Transformer [package=transformer]
  R2 = Resistor [tolerance=±5% resistance=220 power=0.25W package="0603 [SMD]"]
  LED1 = LED - 5mm [color="Red (633nm)" current=0.030 package="5 mm [THT]"]
  R3 = Resistor [tolerance=±5% power=0.25 resistance=220 package=THT]
  Gnd = BANANA_CONN [package=banana_conn]
  +5v = BANANA_CONN [package=banana_conn]
  +_Adjustable = BANANA_CONN [package=banana_conn]
  Gnd_2 = BANANA_CONN [package=banana_conn]

nets:
  N1: D1.cathode, D3.anode, U1.3
  GND: D1.anode, D4.anode, C1.-, C2.-, 7805CT.GND, C3.-, R1.wiper, LED1.cathode, Gnd.1, Gnd_2.1
  N2: D2.cathode, D3.cathode, C1.+, C2.+, 7805CT.input_voltage, LM317K.IN
  N3: D2.anode, D4.cathode, U1.4
  N4: 7805CT.output_voltage, R3.Pin_1, +5v.1
  N5: LM317K.ADJ, R1.leg1, R2.Pin_1
  N6: LM317K.OUT, C3.+, R2.Pin_0, +_Adjustable.1
  N7: Fuse1.Connector1, Part1.L2, Part1_2.L2
  N8: Fuse1.Connector2, U1.1
  N9: Part1.L1, Part1_2.L1
  N10: LED1.anode, R3.Pin_0
